// Logisim project Group7_PartA.circ as structural Verilog
module project_alu (
  input  [3:0] AUSel,
  input  [15:0] A,
  input  [15:0] B,
  input  [2:0] RUSel,
  input  oe,
  output [15:0] AUResult,
  output [15:0] AUDout,
  output RUResult
);

  project_ao project_ao_1 (.A(A), .B(B), .AUSel(AUSel), .AUResult(AUResult));  // open: in_4, in_5, in_6, in_7
  project_ro project_ro_1 (.A(A), .B(B), .RUSel(RUSel), .RUResult(RUResult));
  assign AUDout = oe ? AUResult : 16'bz;  // Controlled_Buffer controlled_buffer_1

  // Notes on the sheet:
  //   Part 1: Arithmetic Logic Unit (ALU) 
  //   16-bit ALU
endmodule

module project_ao (
  input  [15:0] A,
  input  [15:0] B,
  input  [3:0] AUSel,
  input  [3:0] in_4,
  input  [3:0] in_5,
  input  [3:0] in_6,
  input  [3:0] in_7,
  output [15:0] AUResult
);

  wire [15:0] adder_1_out, adder_2_out, and_1_out, divider_1_out, divider_2_out, multiplier_1_out,
       negator_1_out, negator_2_out, not_1_out, or_1_out, shifter_1_out, shifter_2_out, shifter_3_out,
       shifter_4_out, xor_1_out;

  assign not_1_out = ~B;  // NOT_Gate not_1, 16 bits wide
  Adder #(.width(16)) adder_1 (.a(A), .b(B), .out(adder_1_out));  // open: cin, cout
  assign and_1_out = A & B;  // AND_Gate and_1, 16 bits wide
  assign or_1_out = A | B;  // OR_Gate or_1, 16 bits wide
  assign xor_1_out = A ^ B;  // XOR_Gate xor_1, 16 bits wide
  Divider #(.width(16)) divider_1 (.a(A), .b(B), .out(divider_1_out));  // open: upper, rem
  Divider #(.width(16)) divider_2 (.a(A), .b(B), .out(divider_2_out));  // open: upper, rem
  Multiplier #(.width(16)) multiplier_1 (.a(A), .b(B), .out(multiplier_1_out));  // open: cin, cout
  Adder #(.width(16)) adder_2 (.a(A), .b(not_1_out), .out(adder_2_out));  // open: cin, cout
  Shifter #(.width(16)) shifter_1 (.in(A), .\dist (in_4), .out(shifter_1_out));
  Shifter #(.shift("lr"), .width(16)) shifter_2 (.in(A), .\dist (in_7), .out(shifter_2_out));
  Shifter #(.width(16)) shifter_3 (.in(B), .\dist (in_5), .out(shifter_3_out));
  Shifter #(.shift("lr"), .width(16)) shifter_4 (.in(B), .\dist (in_6), .out(shifter_4_out));
  Negator #(.width(16)) negator_1 (.in(A), .out(negator_1_out));
  Negator #(.width(16)) negator_2 (.in(B), .out(negator_2_out));
  Multiplexer #(.select(4), .width(16)) multiplexer_1 (
    .in0(adder_1_out), .in1(and_1_out), .in2(or_1_out), .in3(xor_1_out), .in4(divider_1_out),
    .in5(divider_2_out), .in6(multiplier_1_out), .in7(adder_2_out), .in8(shifter_1_out), .in9(shifter_3_out),
    .in10(shifter_2_out), .in11(shifter_4_out), .in12(negator_1_out), .in13(negator_2_out), .out(AUResult),
    .sel(AUSel));  // open: in14, in15

  // Notes on the sheet:
  //   Part 1: Arithmetic Logic Unit (ALU)
  //   Arithmetic Operation Circuit
endmodule

module project_ro (
  input  [15:0] A,
  input  [15:0] B,
  input  [2:0] RUSel,
  output RUResult
);

  wire comparator_1_eq, comparator_1_gt, comparator_1_lt, not_1_out, or_1_out, or_2_out;

  Comparator #(.width(16)) comparator_1 (
    .a(A), .b(B), .gt(comparator_1_gt), .eq(comparator_1_eq), .lt(comparator_1_lt));
  or or_1 (or_1_out, comparator_1_gt, comparator_1_eq);
  or or_2 (or_2_out, comparator_1_lt, comparator_1_eq);
  not not_1 (not_1_out, comparator_1_eq);
  Multiplexer #(.select(3)) multiplexer_1 (
    .in0(comparator_1_gt), .in1(comparator_1_eq), .in2(or_1_out), .in3(comparator_1_lt), .in4(or_2_out),
    .in5(not_1_out), .out(RUResult), .sel(RUSel));  // open: in6, in7

  // Notes on the sheet:
  //   Part 1: Arithmetic Logic Unit (ALU)
  //   Relational Operation Circuit
endmodule

module reg_8bits (
  input  [7:0] data,
  input  we,
  input  reset,
  input  oe,
  input  clock,
  output [7:0] result,
  output [7:0] dout
);

  Register register_1 (.D(data), .en(we), .clk(clock), .Q(result), .clr(reset));
  assign dout = oe ? result : 8'bz;  // Controlled_Buffer controlled_buffer_1

  // Notes on the sheet:
  //   Part 2: Registers
  //   8-bit Register
endmodule

module reg_16bits (
  input  [15:0] data,
  input  we,
  input  oe,
  input  clock,
  input  reset,
  output [15:0] result,
  output [15:0] dout,
  output [7:0] eight_LSBs,
  output [7:0] eight_MSBs
);

  Register #(.width(16)) register_1 (.D(data), .en(we), .clk(clock), .Q(result), .clr(reset));
  assign dout = oe ? result : 16'bz;  // Controlled_Buffer controlled_buffer_1
  BitSelector #(.group(8), .width(16)) bitselector_1 (.in(dout), .out(eight_LSBs), .sel(1'b0));
  BitSelector #(.group(8), .width(16)) bitselector_2 (.in(dout), .out(eight_MSBs), .sel(1'b1));
endmodule

module Datapath (
  input  we_MAR,
  input  reset_MAR,
  input  [15:0] test,
  input  oe,
  input  we_ir,
  input  reset_ir,
  input  in_7,
  input  oe_ir,
  input  we_regA,
  input  we_MBR,
  input  reset_regA,
  input  reset_MBR,
  input  oe_MBR,
  input  [3:0] AUSel,
  input  [2:0] RUSel,
  input  oe_ALU,
  input  we_regB,
  input  reset_regB,
  input  we_OR,
  input  reset_OR,
  input  oe_OR,
  output [7:0] ouput_MAR,
  output [15:0] ouput_ir,
  output [15:0] out_24,
  output [15:0] ouput_regA,
  output [15:0] output_ALU,
  output RUResult,
  output [15:0] output_regB,
  output [15:0] out_29
);

  wire clock_1_out;
  wire [7:0] bitselector_1_out, MAR_result;
  wire [15:0] ALU_audout, IR_dout;

  Clock clock_1 (.out(clock_1_out));
  reg_16bits IR (
    .data(ALU_audout), .we(we_ir), .oe(oe_ir), .clock(clock_1_out), .reset(reset_ir), .result(ouput_ir),
    .dout(IR_dout));  // open: eight_LSBs, eight_MSBs
  reg_16bits regA (
    .data(ALU_audout), .we(we_regA), .clock(clock_1_out), .reset(reset_regA), .result(ouput_regA));  // open: oe, dout, eight_LSBs, eight_MSBs
  project_alu ALU (
    .AUSel(AUSel), .A(ouput_regA), .B(output_regB), .RUSel(RUSel), .oe(oe_ALU), .AUResult(output_ALU),
    .AUDout(ALU_audout), .RUResult(RUResult));
  reg_16bits regB (
    .data(ALU_audout), .we(we_regB), .clock(clock_1_out), .reset(reset_regB), .result(output_regB));  // open: oe, dout, eight_LSBs, eight_MSBs
  LED D14 (.in(ALU_audout[14]));
  LED D15 (.in(ALU_audout[15]));
  BitSelector #(.group(8), .width(16)) bitselector_1 (.in(IR_dout), .out(bitselector_1_out), .sel(1'b1));
  LED D12 (.in(ALU_audout[12]));
  LED D11 (.in(ALU_audout[11]));
  LED D13 (.in(ALU_audout[13]));
  LED D10 (.in(ALU_audout[10]));
  LED D9 (.in(ALU_audout[9]));
  LED D8 (.in(ALU_audout[8]));
  assign ALU_audout = oe ? test : 16'bz;  // Controlled_Buffer controlled_buffer_1
  assign ALU_audout = in_7 ? out_24 : 16'bz;  // Controlled_Buffer controlled_buffer_2
  reg_8bits MAR (
    .data(bitselector_1_out), .we(we_MAR), .reset(reset_MAR), .clock(clock_1_out), .result(MAR_result),
    .dout(ouput_MAR));  // open: oe
  reg_16bits MBR (
    .data(ALU_audout), .we(we_MBR), .oe(oe_MBR), .clock(clock_1_out), .reset(reset_MBR), .result(out_24),
    .dout(ALU_audout));  // open: eight_LSBs, eight_MSBs
  LED D7 (.in(ALU_audout[7]));
  reg_16bits outputRegister (
    .data(ALU_audout), .we(we_OR), .oe(oe_OR), .clock(clock_1_out), .reset(reset_OR), .result(out_29),
    .dout(ALU_audout));  // open: eight_LSBs, eight_MSBs
  LED D6 (.in(ALU_audout[6]));
  LED D5 (.in(ALU_audout[5]));
  LED D4 (.in(ALU_audout[4]));
  LED D3 (.in(ALU_audout[3]));
  LED D2 (.in(ALU_audout[2]));
  LED D1 (.in(ALU_audout[1]));
  LED D0 (.in(ALU_audout[0]));
  LED led_1 (.in(ALU_audout[15]));
  LED led_2 (.in(ALU_audout[12]));
  LED led_3 (.in(ALU_audout[14]));
  LED led_4 (.in(ALU_audout[13]));
  LED led_5 (.in(ALU_audout[10]));
  LED led_6 (.in(ALU_audout[11]));
  LED led_7 (.in(ALU_audout[8]));
  LED led_8 (.in(ALU_audout[9]));
  LED led_9 (.in(ALU_audout[7]));
  LED led_10 (.in(ALU_audout[6]));
  LED led_11 (.in(ALU_audout[4]));
  LED led_12 (.in(ALU_audout[5]));
  LED led_13 (.in(ALU_audout[2]));
  LED led_14 (.in(ALU_audout[3]));
  LED led_15 (.in(ALU_audout[0]));
  LED led_16 (.in(ALU_audout[1]));

  // Notes on the sheet:
  //   Internal Address Bus
  //   External Address Bus
  //   Part 3: Designing 16-bit CPU Datapath. 
  //   External Address Bus
  //   External Address Bus
endmodule

module CPU (
  input  [7:0] in_1,
  input  in_2,
  input  reset_MAR,
  input  [15:0] test,
  input  oe,
  input  reset_ir,
  input  reset_regA,
  input  reset_MBR,
  input  [3:0] AUSel,
  input  [2:0] RUSel,
  input  reset_regB,
  input  reset_OR,
  output [3:0] out_13,
  output [7:0] ouput_MAR,
  output [15:0] ouput_ir,
  output [15:0] out_16,
  output [15:0] ouput_regA,
  output [15:0] output_ALU,
  output RUResult,
  output [15:0] output_regB,
  output [15:0] out_21,
  output [2:0] out_22
);

  wire clock_1_out, controlunit_1_c0, controlunit_1_c1, controlunit_1_c2, controlunit_1_c3, controlunit_1_c4,
       controlunit_1_c5, controlunit_1_c6, controlunit_1_c7, controlunit_1_c8, controlunit_1_c9,
       controlunit_1_c10, controlunit_1_c11, controlunit_1_c12, controlunit_1_c13, controlunit_1_c14,
       controlunit_1_c15;
  wire [3:0] controlled_buffer_1_out, decimal_decoder16bits_1_dout_3, decimal_decoder16bits_1_dout_4,
       decimal_decoder16bits_2_dout_3, decimal_decoder16bits_2_dout_4, decimal_decoder16bits_3_dout_2,
       decimal_decoder16bits_3_dout_3, decimal_decoder16bits_3_dout_4, decimal_decoder16bits_3_dout_5,
       decimal_decoder16bits_4_dout_3, decimal_decoder16bits_4_dout_4, decimal_decoder16bits_5_dout_2,
       decimal_decoder16bits_5_dout_3, decimal_decoder16bits_5_dout_4, decimal_decoder16bits_5_dout_5;
  wire [7:0] bitselector_2_out, decimal_decoder16bits_1_dout_2, decimal_decoder16bits_2_dout_2,
       decimal_decoder16bits_4_dout_2, MAR_result;
  wire [7:4] bitselector_1_out;
  wire [15:0] ALU_audout, bit_extender_1_out, bit_extender_2_out, decimal_decoder16bits_1_dout,
       decimal_decoder16bits_2_dout, decimal_decoder16bits_3_dout, decimal_decoder16bits_4_dout,
       decimal_decoder16bits_5_dout, IR_dout, RAM_component_dout;
  wire [15:1] undriven;

  _7_Segment_Display u_7_segment_display_1 (
    .g(decimal_decoder16bits_1_dout[15]), .f(decimal_decoder16bits_1_dout[14]),
    .a(decimal_decoder16bits_1_dout[13]), .b(decimal_decoder16bits_1_dout[12]),
    .e(decimal_decoder16bits_1_dout_4[3]), .d(decimal_decoder16bits_1_dout_4[2]),
    .c(decimal_decoder16bits_1_dout_4[1]), .dp(decimal_decoder16bits_1_dout_4[0]));
  _7_Segment_Display u_7_segment_display_2 (
    .g(decimal_decoder16bits_2_dout[15]), .f(decimal_decoder16bits_2_dout[14]),
    .a(decimal_decoder16bits_2_dout[13]), .b(decimal_decoder16bits_2_dout[12]),
    .e(decimal_decoder16bits_2_dout_4[3]), .d(decimal_decoder16bits_2_dout_4[2]),
    .c(decimal_decoder16bits_2_dout_4[1]), .dp(decimal_decoder16bits_2_dout_4[0]));
  _7_Segment_Display u_7_segment_display_3 (
    .g(decimal_decoder16bits_1_dout[11]), .f(decimal_decoder16bits_1_dout[10]),
    .a(decimal_decoder16bits_1_dout[9]), .b(decimal_decoder16bits_1_dout[8]),
    .e(decimal_decoder16bits_1_dout_3[3]), .d(decimal_decoder16bits_1_dout_3[2]),
    .c(decimal_decoder16bits_1_dout_3[1]), .dp(decimal_decoder16bits_1_dout_3[0]));
  _7_Segment_Display u_7_segment_display_4 (
    .g(decimal_decoder16bits_2_dout[11]), .f(decimal_decoder16bits_2_dout[10]),
    .a(decimal_decoder16bits_2_dout[9]), .b(decimal_decoder16bits_2_dout[8]),
    .e(decimal_decoder16bits_2_dout_3[3]), .d(decimal_decoder16bits_2_dout_3[2]),
    .c(decimal_decoder16bits_2_dout_3[1]), .dp(decimal_decoder16bits_2_dout_3[0]));
  _7_Segment_Display u_7_segment_display_5 (
    .g(decimal_decoder16bits_1_dout[7]), .f(decimal_decoder16bits_1_dout[6]),
    .a(decimal_decoder16bits_1_dout[5]), .b(decimal_decoder16bits_1_dout[4]),
    .e(decimal_decoder16bits_1_dout_2[7]), .d(decimal_decoder16bits_1_dout_2[6]),
    .c(decimal_decoder16bits_1_dout_2[5]), .dp(decimal_decoder16bits_1_dout_2[4]));
  _7_Segment_Display u_7_segment_display_6 (
    .g(decimal_decoder16bits_2_dout[7]), .f(decimal_decoder16bits_2_dout[6]),
    .a(decimal_decoder16bits_2_dout[5]), .b(decimal_decoder16bits_2_dout[4]),
    .e(decimal_decoder16bits_2_dout_2[7]), .d(decimal_decoder16bits_2_dout_2[6]),
    .c(decimal_decoder16bits_2_dout_2[5]), .dp(decimal_decoder16bits_2_dout_2[4]));
  Counter #(.max('h3), .width(4)) programCounter (
    .count(controlunit_1_c1), .clk(clock_1_out), .D(controlled_buffer_1_out), .Q(out_13));  // open: clr, load, up, carry
  decimal_decoder16bits decimal_decoder16bits_1 (
    .Din(ouput_regA),
    .Dout({decimal_decoder16bits_1_dout_4, decimal_decoder16bits_1_dout_3, decimal_decoder16bits_1_dout_2, decimal_decoder16bits_1_dout}));
  _7_Segment_Display u_7_segment_display_7 (
    .g(decimal_decoder16bits_1_dout[3]), .f(decimal_decoder16bits_1_dout[2]),
    .a(decimal_decoder16bits_1_dout[1]), .b(decimal_decoder16bits_1_dout[0]),
    .e(decimal_decoder16bits_1_dout_2[3]), .d(decimal_decoder16bits_1_dout_2[2]),
    .c(decimal_decoder16bits_1_dout_2[1]), .dp(decimal_decoder16bits_1_dout_2[0]));
  decimal_decoder16bits decimal_decoder16bits_2 (
    .Din(output_regB),
    .Dout({decimal_decoder16bits_2_dout_4, decimal_decoder16bits_2_dout_3, decimal_decoder16bits_2_dout_2, decimal_decoder16bits_2_dout}));
  _7_Segment_Display u_7_segment_display_8 (
    .g(decimal_decoder16bits_2_dout[3]), .f(decimal_decoder16bits_2_dout[2]),
    .a(decimal_decoder16bits_2_dout[1]), .b(decimal_decoder16bits_2_dout[0]),
    .e(decimal_decoder16bits_2_dout_2[3]), .d(decimal_decoder16bits_2_dout_2[2]),
    .c(decimal_decoder16bits_2_dout_2[1]), .dp(decimal_decoder16bits_2_dout_2[0]));
  Clock clock_1 (.out(clock_1_out));
  assign controlled_buffer_1_out = controlunit_1_c0 ? out_13 : 4'bz;  // Controlled_Buffer controlled_buffer_1
  _7_Segment_Display u_7_segment_display_9 (
    .g(decimal_decoder16bits_3_dout[3]), .f(decimal_decoder16bits_3_dout[2]),
    .a(decimal_decoder16bits_3_dout[1]), .b(decimal_decoder16bits_3_dout[0]),
    .e(decimal_decoder16bits_3_dout_2[3]), .d(decimal_decoder16bits_3_dout_2[2]),
    .c(decimal_decoder16bits_3_dout_2[1]), .dp(decimal_decoder16bits_3_dout_2[0]));
  assign bit_extender_1_out = {{12{1'b0}}, out_13};  // Bit_Extender bit_extender_1
  decimal_decoder16bits decimal_decoder16bits_3 (
    .Din(bit_extender_1_out),
    .Dout({decimal_decoder16bits_3_dout_5, decimal_decoder16bits_3_dout_4, decimal_decoder16bits_3_dout_3, decimal_decoder16bits_3_dout_2, decimal_decoder16bits_3_dout}));
  reg_16bits IR (
    .data(ALU_audout), .we(controlunit_1_c7), .oe(controlunit_1_c8), .clock(clock_1_out), .reset(reset_ir),
    .result(ouput_ir), .dout(IR_dout));  // open: eight_LSBs, eight_MSBs
  reg_16bits regA (
    .data(ALU_audout), .we(controlunit_1_c12), .clock(clock_1_out), .reset(reset_regA), .result(ouput_regA));  // open: oe, dout, eight_LSBs, eight_MSBs
  project_alu ALU (
    .AUSel(AUSel), .A(ouput_regA), .B(output_regB), .RUSel(RUSel), .oe(controlunit_1_c11),
    .AUResult(output_ALU), .AUDout(ALU_audout), .RUResult(RUResult));
  reg_16bits regB (
    .data(ALU_audout), .we(controlunit_1_c13), .clock(clock_1_out), .reset(reset_regB), .result(output_regB));  // open: oe, dout, eight_LSBs, eight_MSBs
  LED D14 (.in(ALU_audout[14]));
  LED D15 (.in(ALU_audout[15]));
  BitSelector #(.group(8), .width(16)) bitselector_1 (
    .in(IR_dout), .out({bitselector_1_out, controlled_buffer_1_out}), .sel(1'b1));
  LED D12 (.in(ALU_audout[12]));
  LED D11 (.in(ALU_audout[11]));
  LED D13 (.in(ALU_audout[13]));
  LED D10 (.in(ALU_audout[10]));
  LED D9 (.in(ALU_audout[9]));
  LED D8 (.in(ALU_audout[8]));
  assign ALU_audout = oe ? test : 16'bz;  // Controlled_Buffer controlled_buffer_2
  assign ALU_audout = controlunit_1_c5 ? out_16 : 16'bz;  // Controlled_Buffer controlled_buffer_3
  reg_8bits MAR (
    .data({bitselector_1_out, controlled_buffer_1_out}), .we(controlunit_1_c9), .reset(reset_MAR),
    .oe(controlunit_1_c10), .clock(clock_1_out), .result(MAR_result), .dout(ouput_MAR));
  reg_16bits MBR (
    .data(ALU_audout), .we(controlunit_1_c4), .oe(controlunit_1_c6), .clock(clock_1_out), .reset(reset_MBR),
    .result(out_16), .dout(ALU_audout));  // open: eight_LSBs, eight_MSBs
  LED D7 (.in(ALU_audout[7]));
  assign MAR_result = in_2 ? in_1 : 8'bz;  // Controlled_Buffer controlled_buffer_4
  reg_16bits outputRegister (
    .data(ALU_audout), .we(controlunit_1_c15), .oe(controlunit_1_c14), .clock(clock_1_out), .reset(reset_OR),
    .result(out_21), .dout(ALU_audout));  // open: eight_LSBs, eight_MSBs
  LED D6 (.in(ALU_audout[6]));
  LED D5 (.in(ALU_audout[5]));
  LED D4 (.in(ALU_audout[4]));
  LED D3 (.in(ALU_audout[3]));
  LED D2 (.in(ALU_audout[2]));
  LED D1 (.in(ALU_audout[1]));
  LED D0 (.in(ALU_audout[0]));
  LED led_1 (.in(ALU_audout[15]));
  _7_Segment_Display u_7_segment_display_10 (
    .g(decimal_decoder16bits_4_dout[15]), .f(decimal_decoder16bits_4_dout[14]),
    .a(decimal_decoder16bits_4_dout[13]), .b(decimal_decoder16bits_4_dout[12]),
    .e(decimal_decoder16bits_4_dout_4[3]), .d(decimal_decoder16bits_4_dout_4[2]),
    .c(decimal_decoder16bits_4_dout_4[1]), .dp(decimal_decoder16bits_4_dout_4[0]));
  LED led_2 (.in(ALU_audout[12]));
  LED led_3 (.in(ALU_audout[14]));
  LED led_4 (.in(ALU_audout[13]));
  _7_Segment_Display u_7_segment_display_11 (
    .g(decimal_decoder16bits_4_dout[11]), .f(decimal_decoder16bits_4_dout[10]),
    .a(decimal_decoder16bits_4_dout[9]), .b(decimal_decoder16bits_4_dout[8]),
    .e(decimal_decoder16bits_4_dout_3[3]), .d(decimal_decoder16bits_4_dout_3[2]),
    .c(decimal_decoder16bits_4_dout_3[1]), .dp(decimal_decoder16bits_4_dout_3[0]));
  LED led_5 (.in(ALU_audout[10]));
  LED led_6 (.in(ALU_audout[11]));
  LED led_7 (.in(ALU_audout[8]));
  LED led_8 (.in(ALU_audout[9]));
  _7_Segment_Display u_7_segment_display_12 (
    .g(decimal_decoder16bits_4_dout[7]), .f(decimal_decoder16bits_4_dout[6]),
    .a(decimal_decoder16bits_4_dout[5]), .b(decimal_decoder16bits_4_dout[4]),
    .e(decimal_decoder16bits_4_dout_2[7]), .d(decimal_decoder16bits_4_dout_2[6]),
    .c(decimal_decoder16bits_4_dout_2[5]), .dp(decimal_decoder16bits_4_dout_2[4]));
  decimal_decoder16bits decimal_decoder16bits_4 (
    .Din(out_21),
    .Dout({decimal_decoder16bits_4_dout_4, decimal_decoder16bits_4_dout_3, decimal_decoder16bits_4_dout_2, decimal_decoder16bits_4_dout}));
  _7_Segment_Display u_7_segment_display_13 (
    .g(decimal_decoder16bits_4_dout[3]), .f(decimal_decoder16bits_4_dout[2]),
    .a(decimal_decoder16bits_4_dout[1]), .b(decimal_decoder16bits_4_dout[0]),
    .e(decimal_decoder16bits_4_dout_2[3]), .d(decimal_decoder16bits_4_dout_2[2]),
    .c(decimal_decoder16bits_4_dout_2[1]), .dp(decimal_decoder16bits_4_dout_2[0]));
  RAM #(.dataWidth(16), .enables("line")) RAM_component (
    .addr(MAR_result), .we(controlunit_1_c2), .clk(clock_1_out), .din({undriven, ALU_audout[0]}),
    .dout(RAM_component_dout));
  Controlled_Buffer #(.width(16)) controlled_buffer_5 (.in(RAM_component_dout), .en(controlunit_1_c3));  // open: out
  LED led_9 (.in(ALU_audout[7]));
  LED led_10 (.in(ALU_audout[6]));
  LED led_11 (.in(ALU_audout[4]));
  LED led_12 (.in(ALU_audout[5]));
  LED led_13 (.in(ALU_audout[2]));
  LED led_14 (.in(ALU_audout[3]));
  LED led_15 (.in(ALU_audout[0]));
  LED led_16 (.in(ALU_audout[1]));
  decimal_decoder16bits decimal_decoder16bits_5 (
    .Din(bit_extender_2_out),
    .Dout({decimal_decoder16bits_5_dout_5, decimal_decoder16bits_5_dout_4, decimal_decoder16bits_5_dout_3, decimal_decoder16bits_5_dout_2, decimal_decoder16bits_5_dout}));
  _7_Segment_Display u_7_segment_display_14 (
    .g(decimal_decoder16bits_5_dout[3]), .f(decimal_decoder16bits_5_dout[2]),
    .a(decimal_decoder16bits_5_dout[1]), .b(decimal_decoder16bits_5_dout[0]),
    .e(decimal_decoder16bits_5_dout_2[3]), .d(decimal_decoder16bits_5_dout_2[2]),
    .c(decimal_decoder16bits_5_dout_2[1]), .dp(decimal_decoder16bits_5_dout_2[0]));
  assign bit_extender_2_out = {{13{out_22[2]}}, out_22};  // Bit_Extender bit_extender_2
  BitSelector #(.group(8), .width(16)) bitselector_2 (.in(ouput_ir), .out(bitselector_2_out), .sel(1'b1));
  Counter #(.max('h5), .width(3)) step_counter (.clk(clock_1_out), .Q(out_22));  // open: clr, load, up, count, D, carry
  ControlUnit controlunit_1 (
    .OPC7(bitselector_2_out[7]), .OPC6(bitselector_2_out[1]), .OPC5(bitselector_2_out[2]),
    .OPC4(bitselector_2_out[3]), .OPC3(bitselector_2_out[4]), .OPC2(bitselector_2_out[5]),
    .OPC1(bitselector_2_out[6]), .OPC0(bitselector_2_out[0]), .SC2(out_22[2]), .SC1(out_22[1]),
    .SC0(out_22[0]), .C0(controlunit_1_c0), .C1(controlunit_1_c1), .C2(controlunit_1_c2),
    .C3(controlunit_1_c3), .C4(controlunit_1_c4), .C5(controlunit_1_c5), .C6(controlunit_1_c6),
    .C7(controlunit_1_c7), .C8(controlunit_1_c8), .C9(controlunit_1_c9), .C10(controlunit_1_c10),
    .C11(controlunit_1_c11), .C12(controlunit_1_c12), .C13(controlunit_1_c13), .C14(controlunit_1_c14),
    .C15(controlunit_1_c15));

  // Notes on the sheet:
  //   Internal Address Bus
  //   External Address Bus
  //   External Address Bus
  //   External Address Bus
endmodule

module decimal_decoder16bits (
  input  [15:0] Din,
  output [31:0] Dout
);

  ROM #(.addrWidth(16), .dataWidth(32)) Decimal_Decoder (
    .addr(Din),
    .data({Dout[31:28], Dout[15:12], Dout[27:24], Dout[11:8], Dout[23:20], Dout[7:4], Dout[19:16], Dout[3:0]}));

  // Notes on the sheet:
  //   contents of Decimal_Decoder (hex, n*v repeats v):
  //   e7 21 cb 6b 2d 6e ee 23 ef 2f 21e7 2121 21cb 216b 212d 216e 21ee 2123 21ef 212f cbe7 cb21 cbcb cb6b
  //   cb2d cb6e cbee cb23 cbef cb2f 6be7 6b21 6bcb 6b6b 6b2d 6b6e 6bee 6b23 6bef 6b2f 2de7 2d21 2dcb 2d6b
  //   2d2d 2d6e 2dee 2d23 2def 2d2f 6ee7 6e21 6ecb 6e6b 6e2d 6e6e 6eee 6e23 6eef 6e2f eee7 ee21 eecb ee6b
  //   ee2d ee6e eeee ee23 eeef ee2f 23e7 2321 23cb 236b 232d 236e 23ee 2323 23ef 232f efe7 ef21 efcb ef6b
  //   ef2d ef6e efee ef23 efef ef2f 2fe7 2f21 2fcb 2f6b 2f2d 2f6e 2fee 2f23 2fef 2f2f 21e7e7 21e721 21e7cb
  //   21e76b 21e72d 21e76e 21e7ee 21e723 21e7ef 21e72f 2121e7 212121 2121cb 21216b 21212d 21216e 2121ee
  //   212123 2121ef 21212f 21cbe7 21cb21 21cbcb 21cb6b 21cb2d 21cb6e 21cbee 21cb23 21cbef 21cb2f 216be7
  //   216b21 216bcb 216b6b 216b2d 216b6e 216bee 216b23 216bef 216b2f 212de7 212d21 212dcb 212d6b 212d2d
  //   212d6e 212dee 212d23 212def 212d2f 216ee7 216e21 216ecb 216e6b 216e2d 216e6e 216eee 216e23 216eef
  //   216e2f 21eee7 21ee21 21eecb 21ee6b 21ee2d 21ee6e 21eeee 21ee23 21eeef 21ee2f 2123e7 212321 2123cb
  //   21236b 21232d 21236e 2123ee 212323 2123ef 21232f 21efe7 21ef21 21efcb 21ef6b 21ef2d 21ef6e 21efee
  //   21ef23 21efef 21ef2f 212fe7 212f21 212fcb 212f6b 212f2d 212f6e 212fee 212f23 212fef 212f2f cbe7e7
  //   cbe721 cbe7cb cbe76b cbe72d cbe76e cbe7ee cbe723 cbe7ef cbe72f cb21e7 cb2121 cb21cb cb216b cb212d
  //   cb216e cb21ee cb2123 cb21ef cb212f cbcbe7 cbcb21 cbcbcb cbcb6b cbcb2d cbcb6e cbcbee cbcb23 cbcbef
  //   cbcb2f cb6be7 cb6b21 cb6bcb cb6b6b cb6b2d cb6b6e cb6bee cb6b23 cb6bef cb6b2f cb2de7 cb2d21 cb2dcb
  //   cb2d6b cb2d2d cb2d6e cb2dee cb2d23 cb2def cb2d2f cb6ee7 cb6e21 cb6ecb cb6e6b cb6e2d cb6e6e
  //   Part 4: Designing a Program Counter (PC), 7-segment display and Interfacing RAM.
  //   Decimal Decoder using ROM
endmodule

module ControlUnit (
  input  OPC7,
  input  OPC6,
  input  OPC5,
  input  OPC4,
  input  OPC3,
  input  OPC2,
  input  OPC1,
  input  OPC0,
  input  SC2,
  input  SC1,
  input  SC0,
  output C0,
  output C1,
  output C2,
  output C3,
  output C4,
  output C5,
  output C6,
  output C7,
  output C8,
  output C9,
  output C10,
  output C11,
  output C12,
  output C13,
  output C14,
  output C15
);

  wire and_4_out, and_5_out, and_6_out, and_7_out, and_8_out, and_9_out, and_10_out, and_13_out, and_14_out,
       and_15_out, and_16_out, and_17_out, and_18_out, and_19_out, and_20_out, not_1_out, not_2_out,
       not_3_out, not_4_out, not_5_out;

  not not_1 (not_1_out, OPC1);
  not not_2 (not_2_out, OPC0);
  not not_3 (not_3_out, SC2);
  not not_4 (not_4_out, SC1);
  not not_5 (not_5_out, SC0);
  and and_1 (C0, not_3_out, not_4_out, not_5_out);
  and and_2 (C1, not_3_out, not_4_out, SC0);
  and and_3 (C2, OPC1, OPC0, SC2, not_4_out, not_5_out);
  and and_4 (and_4_out, not_3_out, not_4_out, SC0);
  and and_5 (and_5_out, not_1_out, SC2, not_4_out, not_5_out);
  and and_6 (and_6_out, not_3_out, not_4_out, SC0);
  and and_7 (and_7_out, not_1_out, SC2, not_4_out, not_5_out);
  and and_8 (and_8_out, OPC1, OPC0, not_3_out, SC0);
  and and_9 (and_9_out, not_3_out, SC1, not_5_out);
  and and_10 (and_10_out, not_1_out, SC2, not_4_out, SC0);
  and and_11 (C6, OPC1, OPC0, SC2, not_4_out, not_5_out);
  and and_12 (C7, not_3_out, SC1, not_5_out);
  and and_13 (and_13_out, not_1_out, not_3_out, SC1, SC0);
  and and_14 (and_14_out, OPC0, not_3_out, SC1, SC0);
  and and_15 (and_15_out, not_3_out, not_4_out, not_5_out);
  and and_16 (and_16_out, not_1_out, not_3_out, SC1, SC0);
  and and_17 (and_17_out, OPC0, not_3_out, SC1, SC0);
  and and_18 (and_18_out, not_3_out, not_4_out, SC0);
  and and_19 (and_19_out, not_1_out, SC2, not_4_out, not_5_out);
  and and_20 (and_20_out, OPC0, SC2, not_4_out, not_5_out);
  and and_21 (C11, OPC1, not_2_out, not_3_out, SC1, SC0);
  and and_22 (C12, not_1_out, not_2_out, SC2, not_4_out, SC0);
  and and_23 (C13, not_1_out, OPC0, SC2, not_4_out, SC0);
  and and_24 (C14, OPC1, OPC0, not_3_out, SC1, SC0);
  and and_25 (C15, OPC1, not_2_out, not_3_out, SC1, SC0);
  or or_1 (C3, and_4_out, and_5_out);
  or or_2 (C4, and_6_out, and_7_out, and_8_out);
  or or_3 (C5, and_9_out, and_10_out);
  or or_4 (C8, and_13_out, and_14_out);
  or or_5 (C9, and_15_out, and_16_out, and_17_out);
  or or_6 (C10, and_18_out, and_19_out, and_20_out);

  // Notes on the sheet:
  //   Control Unit
  //   Part 6: Control Signals, Control Unit and Step Counter 
endmodule

module back_up_cpu (
  input  counter_oe,
  input  counter_enable,
  input  [7:0] in_3,
  input  in_4,
  input  we_MAR,
  input  reset_MAR,
  input  [15:0] test,
  input  we,
  input  oe,
  input  o_e,
  input  we_ir,
  input  reset_ir,
  input  in_13,
  input  oe_ir,
  input  we_regA,
  input  we_MBR,
  input  reset_regA,
  input  reset_MBR,
  input  oe_MBR,
  input  [3:0] AUSel,
  input  [2:0] RUSel,
  input  oe_ALU,
  input  we_regB,
  input  reset_regB,
  input  we_OR,
  input  reset_OR,
  input  oe_OR,
  output [3:0] out_28,
  output [7:0] ouput_MAR,
  output [15:0] ouput_ir,
  output [15:0] out_31,
  output [15:0] ouput_regA,
  output [15:0] output_ALU,
  output RUResult,
  output [15:0] output_regB,
  output [15:0] out_36,
  output [2:0] out_37
);

  wire clock_1_out;
  wire [3:0] controlled_buffer_1_out, decimal_decoder16bits_1_dout_3, decimal_decoder16bits_1_dout_4,
       decimal_decoder16bits_2_dout_3, decimal_decoder16bits_2_dout_4, decimal_decoder16bits_3_dout_2,
       decimal_decoder16bits_3_dout_3, decimal_decoder16bits_3_dout_4, decimal_decoder16bits_3_dout_5,
       decimal_decoder16bits_4_dout_3, decimal_decoder16bits_4_dout_4, decimal_decoder16bits_5_dout_2,
       decimal_decoder16bits_5_dout_3, decimal_decoder16bits_5_dout_4, decimal_decoder16bits_5_dout_5;
  wire [7:0] bitselector_2_out, decimal_decoder16bits_1_dout_2, decimal_decoder16bits_2_dout_2,
       decimal_decoder16bits_4_dout_2, MAR_result;
  wire [7:4] bitselector_1_out;
  wire [15:0] ALU_audout, bit_extender_1_out, bit_extender_2_out, decimal_decoder16bits_1_dout,
       decimal_decoder16bits_2_dout, decimal_decoder16bits_3_dout, decimal_decoder16bits_4_dout,
       decimal_decoder16bits_5_dout, IR_dout, RAM_component_dout;
  wire [15:1] undriven;

  _7_Segment_Display u_7_segment_display_1 (
    .g(decimal_decoder16bits_1_dout[15]), .f(decimal_decoder16bits_1_dout[14]),
    .a(decimal_decoder16bits_1_dout[13]), .b(decimal_decoder16bits_1_dout[12]),
    .e(decimal_decoder16bits_1_dout_4[3]), .d(decimal_decoder16bits_1_dout_4[2]),
    .c(decimal_decoder16bits_1_dout_4[1]), .dp(decimal_decoder16bits_1_dout_4[0]));
  _7_Segment_Display u_7_segment_display_2 (
    .g(decimal_decoder16bits_2_dout[15]), .f(decimal_decoder16bits_2_dout[14]),
    .a(decimal_decoder16bits_2_dout[13]), .b(decimal_decoder16bits_2_dout[12]),
    .e(decimal_decoder16bits_2_dout_4[3]), .d(decimal_decoder16bits_2_dout_4[2]),
    .c(decimal_decoder16bits_2_dout_4[1]), .dp(decimal_decoder16bits_2_dout_4[0]));
  _7_Segment_Display u_7_segment_display_3 (
    .g(decimal_decoder16bits_1_dout[11]), .f(decimal_decoder16bits_1_dout[10]),
    .a(decimal_decoder16bits_1_dout[9]), .b(decimal_decoder16bits_1_dout[8]),
    .e(decimal_decoder16bits_1_dout_3[3]), .d(decimal_decoder16bits_1_dout_3[2]),
    .c(decimal_decoder16bits_1_dout_3[1]), .dp(decimal_decoder16bits_1_dout_3[0]));
  _7_Segment_Display u_7_segment_display_4 (
    .g(decimal_decoder16bits_2_dout[11]), .f(decimal_decoder16bits_2_dout[10]),
    .a(decimal_decoder16bits_2_dout[9]), .b(decimal_decoder16bits_2_dout[8]),
    .e(decimal_decoder16bits_2_dout_3[3]), .d(decimal_decoder16bits_2_dout_3[2]),
    .c(decimal_decoder16bits_2_dout_3[1]), .dp(decimal_decoder16bits_2_dout_3[0]));
  _7_Segment_Display u_7_segment_display_5 (
    .g(decimal_decoder16bits_1_dout[7]), .f(decimal_decoder16bits_1_dout[6]),
    .a(decimal_decoder16bits_1_dout[5]), .b(decimal_decoder16bits_1_dout[4]),
    .e(decimal_decoder16bits_1_dout_2[7]), .d(decimal_decoder16bits_1_dout_2[6]),
    .c(decimal_decoder16bits_1_dout_2[5]), .dp(decimal_decoder16bits_1_dout_2[4]));
  _7_Segment_Display u_7_segment_display_6 (
    .g(decimal_decoder16bits_2_dout[7]), .f(decimal_decoder16bits_2_dout[6]),
    .a(decimal_decoder16bits_2_dout[5]), .b(decimal_decoder16bits_2_dout[4]),
    .e(decimal_decoder16bits_2_dout_2[7]), .d(decimal_decoder16bits_2_dout_2[6]),
    .c(decimal_decoder16bits_2_dout_2[5]), .dp(decimal_decoder16bits_2_dout_2[4]));
  Counter #(.max('h3), .width(4)) programCounter (
    .count(counter_enable), .clk(clock_1_out), .D(controlled_buffer_1_out), .Q(out_28));  // open: clr, load, up, carry
  decimal_decoder16bits decimal_decoder16bits_1 (
    .Din(ouput_regA),
    .Dout({decimal_decoder16bits_1_dout_4, decimal_decoder16bits_1_dout_3, decimal_decoder16bits_1_dout_2, decimal_decoder16bits_1_dout}));
  _7_Segment_Display u_7_segment_display_7 (
    .g(decimal_decoder16bits_1_dout[3]), .f(decimal_decoder16bits_1_dout[2]),
    .a(decimal_decoder16bits_1_dout[1]), .b(decimal_decoder16bits_1_dout[0]),
    .e(decimal_decoder16bits_1_dout_2[3]), .d(decimal_decoder16bits_1_dout_2[2]),
    .c(decimal_decoder16bits_1_dout_2[1]), .dp(decimal_decoder16bits_1_dout_2[0]));
  decimal_decoder16bits decimal_decoder16bits_2 (
    .Din(output_regB),
    .Dout({decimal_decoder16bits_2_dout_4, decimal_decoder16bits_2_dout_3, decimal_decoder16bits_2_dout_2, decimal_decoder16bits_2_dout}));
  _7_Segment_Display u_7_segment_display_8 (
    .g(decimal_decoder16bits_2_dout[3]), .f(decimal_decoder16bits_2_dout[2]),
    .a(decimal_decoder16bits_2_dout[1]), .b(decimal_decoder16bits_2_dout[0]),
    .e(decimal_decoder16bits_2_dout_2[3]), .d(decimal_decoder16bits_2_dout_2[2]),
    .c(decimal_decoder16bits_2_dout_2[1]), .dp(decimal_decoder16bits_2_dout_2[0]));
  Clock clock_1 (.out(clock_1_out));
  assign controlled_buffer_1_out = counter_oe ? out_28 : 4'bz;  // Controlled_Buffer controlled_buffer_1
  _7_Segment_Display u_7_segment_display_9 (
    .g(decimal_decoder16bits_3_dout[3]), .f(decimal_decoder16bits_3_dout[2]),
    .a(decimal_decoder16bits_3_dout[1]), .b(decimal_decoder16bits_3_dout[0]),
    .e(decimal_decoder16bits_3_dout_2[3]), .d(decimal_decoder16bits_3_dout_2[2]),
    .c(decimal_decoder16bits_3_dout_2[1]), .dp(decimal_decoder16bits_3_dout_2[0]));
  assign bit_extender_1_out = {{12{1'b0}}, out_28};  // Bit_Extender bit_extender_1
  decimal_decoder16bits decimal_decoder16bits_3 (
    .Din(bit_extender_1_out),
    .Dout({decimal_decoder16bits_3_dout_5, decimal_decoder16bits_3_dout_4, decimal_decoder16bits_3_dout_3, decimal_decoder16bits_3_dout_2, decimal_decoder16bits_3_dout}));
  reg_16bits IR (
    .data(ALU_audout), .we(we_ir), .oe(oe_ir), .clock(clock_1_out), .reset(reset_ir), .result(ouput_ir),
    .dout(IR_dout));  // open: eight_LSBs, eight_MSBs
  reg_16bits regA (
    .data(ALU_audout), .we(we_regA), .clock(clock_1_out), .reset(reset_regA), .result(ouput_regA));  // open: oe, dout, eight_LSBs, eight_MSBs
  project_alu ALU (
    .AUSel(AUSel), .A(ouput_regA), .B(output_regB), .RUSel(RUSel), .oe(oe_ALU), .AUResult(output_ALU),
    .AUDout(ALU_audout), .RUResult(RUResult));
  reg_16bits regB (
    .data(ALU_audout), .we(we_regB), .clock(clock_1_out), .reset(reset_regB), .result(output_regB));  // open: oe, dout, eight_LSBs, eight_MSBs
  LED D14 (.in(ALU_audout[14]));
  LED D15 (.in(ALU_audout[15]));
  BitSelector #(.group(8), .width(16)) bitselector_1 (
    .in(IR_dout), .out({bitselector_1_out, controlled_buffer_1_out}), .sel(1'b1));
  LED D12 (.in(ALU_audout[12]));
  LED D11 (.in(ALU_audout[11]));
  LED D13 (.in(ALU_audout[13]));
  LED D10 (.in(ALU_audout[10]));
  LED D9 (.in(ALU_audout[9]));
  LED D8 (.in(ALU_audout[8]));
  assign ALU_audout = oe ? test : 16'bz;  // Controlled_Buffer controlled_buffer_2
  assign ALU_audout = in_13 ? out_31 : 16'bz;  // Controlled_Buffer controlled_buffer_3
  reg_8bits MAR (
    .data({bitselector_1_out, controlled_buffer_1_out}), .we(we_MAR), .reset(reset_MAR), .clock(clock_1_out),
    .result(MAR_result), .dout(ouput_MAR));  // open: oe
  reg_16bits MBR (
    .data(ALU_audout), .we(we_MBR), .oe(oe_MBR), .clock(clock_1_out), .reset(reset_MBR), .result(out_31),
    .dout(ALU_audout));  // open: eight_LSBs, eight_MSBs
  LED D7 (.in(ALU_audout[7]));
  assign MAR_result = in_4 ? in_3 : 8'bz;  // Controlled_Buffer controlled_buffer_4
  reg_16bits outputRegister (
    .data(ALU_audout), .we(we_OR), .oe(oe_OR), .clock(clock_1_out), .reset(reset_OR), .result(out_36),
    .dout(ALU_audout));  // open: eight_LSBs, eight_MSBs
  LED D6 (.in(ALU_audout[6]));
  LED D5 (.in(ALU_audout[5]));
  LED D4 (.in(ALU_audout[4]));
  LED D3 (.in(ALU_audout[3]));
  LED D2 (.in(ALU_audout[2]));
  LED D1 (.in(ALU_audout[1]));
  LED D0 (.in(ALU_audout[0]));
  LED led_1 (.in(ALU_audout[15]));
  _7_Segment_Display u_7_segment_display_10 (
    .g(decimal_decoder16bits_4_dout[15]), .f(decimal_decoder16bits_4_dout[14]),
    .a(decimal_decoder16bits_4_dout[13]), .b(decimal_decoder16bits_4_dout[12]),
    .e(decimal_decoder16bits_4_dout_4[3]), .d(decimal_decoder16bits_4_dout_4[2]),
    .c(decimal_decoder16bits_4_dout_4[1]), .dp(decimal_decoder16bits_4_dout_4[0]));
  LED led_2 (.in(ALU_audout[12]));
  LED led_3 (.in(ALU_audout[14]));
  LED led_4 (.in(ALU_audout[13]));
  _7_Segment_Display u_7_segment_display_11 (
    .g(decimal_decoder16bits_4_dout[11]), .f(decimal_decoder16bits_4_dout[10]),
    .a(decimal_decoder16bits_4_dout[9]), .b(decimal_decoder16bits_4_dout[8]),
    .e(decimal_decoder16bits_4_dout_3[3]), .d(decimal_decoder16bits_4_dout_3[2]),
    .c(decimal_decoder16bits_4_dout_3[1]), .dp(decimal_decoder16bits_4_dout_3[0]));
  LED led_5 (.in(ALU_audout[10]));
  LED led_6 (.in(ALU_audout[11]));
  LED led_7 (.in(ALU_audout[8]));
  LED led_8 (.in(ALU_audout[9]));
  _7_Segment_Display u_7_segment_display_12 (
    .g(decimal_decoder16bits_4_dout[7]), .f(decimal_decoder16bits_4_dout[6]),
    .a(decimal_decoder16bits_4_dout[5]), .b(decimal_decoder16bits_4_dout[4]),
    .e(decimal_decoder16bits_4_dout_2[7]), .d(decimal_decoder16bits_4_dout_2[6]),
    .c(decimal_decoder16bits_4_dout_2[5]), .dp(decimal_decoder16bits_4_dout_2[4]));
  decimal_decoder16bits decimal_decoder16bits_4 (
    .Din(out_36),
    .Dout({decimal_decoder16bits_4_dout_4, decimal_decoder16bits_4_dout_3, decimal_decoder16bits_4_dout_2, decimal_decoder16bits_4_dout}));
  _7_Segment_Display u_7_segment_display_13 (
    .g(decimal_decoder16bits_4_dout[3]), .f(decimal_decoder16bits_4_dout[2]),
    .a(decimal_decoder16bits_4_dout[1]), .b(decimal_decoder16bits_4_dout[0]),
    .e(decimal_decoder16bits_4_dout_2[3]), .d(decimal_decoder16bits_4_dout_2[2]),
    .c(decimal_decoder16bits_4_dout_2[1]), .dp(decimal_decoder16bits_4_dout_2[0]));
  RAM #(.dataWidth(16), .enables("line")) RAM_component (
    .addr(MAR_result), .we(we), .clk(clock_1_out), .din({undriven, ALU_audout[0]}), .dout(RAM_component_dout));
  Controlled_Buffer #(.width(16)) controlled_buffer_5 (.in(RAM_component_dout), .en(o_e));  // open: out
  LED led_9 (.in(ALU_audout[7]));
  LED led_10 (.in(ALU_audout[6]));
  LED led_11 (.in(ALU_audout[4]));
  LED led_12 (.in(ALU_audout[5]));
  LED led_13 (.in(ALU_audout[2]));
  LED led_14 (.in(ALU_audout[3]));
  LED led_15 (.in(ALU_audout[0]));
  LED led_16 (.in(ALU_audout[1]));
  decimal_decoder16bits decimal_decoder16bits_5 (
    .Din(bit_extender_2_out),
    .Dout({decimal_decoder16bits_5_dout_5, decimal_decoder16bits_5_dout_4, decimal_decoder16bits_5_dout_3, decimal_decoder16bits_5_dout_2, decimal_decoder16bits_5_dout}));
  _7_Segment_Display u_7_segment_display_14 (
    .g(decimal_decoder16bits_5_dout[3]), .f(decimal_decoder16bits_5_dout[2]),
    .a(decimal_decoder16bits_5_dout[1]), .b(decimal_decoder16bits_5_dout[0]),
    .e(decimal_decoder16bits_5_dout_2[3]), .d(decimal_decoder16bits_5_dout_2[2]),
    .c(decimal_decoder16bits_5_dout_2[1]), .dp(decimal_decoder16bits_5_dout_2[0]));
  assign bit_extender_2_out = {{13{out_37[2]}}, out_37};  // Bit_Extender bit_extender_2
  BitSelector #(.group(8), .width(16)) bitselector_2 (.in(ouput_ir), .out(bitselector_2_out), .sel(1'b1));
  Counter #(.max('h5), .width(3)) step_counter (.Q(out_37));  // open: clr, load, up, count, clk, D, carry
  ControlUnit controlunit_1 (
    .OPC7(bitselector_2_out[7]), .OPC6(bitselector_2_out[1]), .OPC5(bitselector_2_out[2]),
    .OPC4(bitselector_2_out[3]), .OPC3(bitselector_2_out[4]), .OPC2(bitselector_2_out[5]),
    .OPC1(bitselector_2_out[6]), .OPC0(bitselector_2_out[0]), .SC2(out_37[2]), .SC1(out_37[1]),
    .SC0(out_37[0]));  // open: C0, C1, C2, C3, C4, C5, C6, C7, C8, C9, C10, C11, C12, C13, C14, C15

  // Notes on the sheet:
  //   Internal Address Bus
  //   External Address Bus
  //   External Address Bus
  //   External Address Bus
endmodule
